# Fritzing sketch EngineEmulator (saved by Fritzing 0.8.0b)
stripboards: 1

parts:
  J1 = male pin header, 4 pins [form="♂ (male)"]
  LED1 = LED - 5mm [color="Red (633nm)" package="5 mm [THT]"]
  LED2 = LED - 5mm [color="Red (633nm)" package="5 mm [THT]"]
  LED3 = LED - 5mm [color="Yellow (595nm)" package="5 mm [THT]"]
  LED4 = LED - 5mm [color="Yellow (595nm)" package="5 mm [THT]"]
  R1 = Resistor [tolerance=±5% resistance=220 package=THT]
  R2 = Resistor [tolerance=±5% resistance=220 package=THT]
  R4 = Resistor [tolerance=±5% resistance=220 package=THT]
  R5 = Resistor [tolerance=±5% resistance=220 package=THT]

nets:
  N1: J1.pin1, LED4.anode, R5.Pin_0
  N2: J1.pin2, LED1.anode, R1.Pin_0
  N3: J1.pin3, LED3.anode, R4.Pin_1
  N4: J1.pin4, LED2.anode, R2.Pin_1
  N5: LED1.cathode, R5.Pin_1
  N6: LED2.cathode, R4.Pin_0
  N7: LED3.cathode, R2.Pin_0
  N8: LED4.cathode, R1.Pin_1
