# Fritzing sketch PhotoResitorTest (saved by Fritzing 0.8.0b)
breadboards: 1

parts:
  Part1 = Arduino Uno (Rev3)
  R1 = Resistor [tolerance=±5% resistance=10k package=THT]
  R2 = Photocell (LDR) [package=THT]
  LED1 = LED - 5mm [color="Yellow (585nm)" package="5 mm [THT]"]
  R3 = Resistor [tolerance=±5% resistance=220 package=THT]

nets:
  N1: Part1.A0, R1.Pin_0, R2.pin_0
  N2: Part1.GND, R1.Pin_1, R3.Pin_0
  N3: Part1.D3_PWM, LED1.anode
  N4: Part1.5V, R2.pin_1
  N5: LED1.cathode, R3.Pin_1
