# Fritzing sketch Robot_Drive_v0.4.1 (saved by Fritzing 0.8.0b)
stripboards: 3

parts:
  Left_Drive = DC Motor [part_number=POL-0992]
  Right_Drive = DC Motor [part_number=POL-0992]
  HDrive = H-Bridge [package=THT]
  C1 = Electrolytic Capacitor [capacitance=1µF package="100 mil [THT, electrolytic]"]
  C2 = Electrolytic Capacitor [capacitance=1µF package="100 mil [THT, electrolytic]"]
  C3 = Electrolytic Capacitor [capacitance=4.7mF package="100 mil [THT, electrolytic]"]
  Fuse1 = Fuse with Handler [part_number=Htc-15m]
  S1 = Pushbutton [package=THT]
  Power = LED - 5mm [color="Red (633nm)" package="5 mm [THT]"]
  R2 = Photocell (LDR) [package=THT]
  R3 = Resistor [tolerance=±5% resistance=10k package=THT]
  R4 = Photocell (LDR) [package=THT]
  R5 = Resistor [tolerance=±5% resistance=10k package=THT]
  U1 = Voltage Regulator - 5V [part_number=L7806CV package="TO220 [THT]"]
  R1 = Resistor [tolerance=±5% resistance=220 package=THT]
  Arduino_RobotDriver = Arduino
  C4 = Electrolytic Capacitor [capacitance=100nF package="100 mil [THT, electrolytic]"]
  J2 = male pin header, 3 pins [form="♂ (male)"]
  J1 = male pin header, 3 pins [form="♂ (male)"]
  J3 = male pin header, 2 pins [form="♂ (male)"]
  J4 = male pin header, 2 pins [form="♂ (male)"]
  S2 = Pushbutton [package=THT]
  VCC2_-_9v_block = Battery block 9V
  J5 = male pin header, 2 pins [form="♂ (male)"]
  J6 = male pin header, 2 pins [form="♂ (male)"]
  J7 = male pin header, 2 pins [form="♂ (male)"]
  J8 = male pin header, 2 pins [form="♂ (male)"]
  VCC1_6xAAA = Battery block 9V

nets:
  N1: Left_Drive.pin_1, HDrive.4Y, C2.-, J3.pin1
  N2: Left_Drive.pin_2, HDrive.3Y, C2.+, J3.pin2
  N3: Right_Drive.pin_1, HDrive.2Y, C1.-, J4.pin1
  N4: Right_Drive.pin_2, HDrive.1Y, C1.+, J4.pin2
  N5: HDrive.1_2EN, Arduino_RobotDriver.D5
  N6: HDrive.1A, Arduino_RobotDriver.D6
  GND: HDrive.GND1, HDrive.GND2, HDrive.GND3, HDrive.GND4, C3.-, R3.Pin_1, R5.Pin_1, U1.GND, R1.Pin_1, Arduino_RobotDriver.GND, C4.-, J2.pin1, J1.pin1, VCC2_-_9v_block.-, J5.pin2, J6.pin1, VCC1_6xAAA.-
  N7: HDrive.2A, Arduino_RobotDriver.D7
  N8: HDrive.VCC2, C3.+, Power.anode, U1.output_voltage, C4.+
  N9: HDrive.3_4EN, Arduino_RobotDriver.D3
  N10: HDrive.3A, Arduino_RobotDriver.D2
  N11: HDrive.4A, Arduino_RobotDriver.D4
  N12: HDrive.VCC1, R2.pin_0, R4.pin_0, Arduino_RobotDriver.+5V, J2.pin3, J1.pin3
  N13: Fuse1.Connector1, S1.leg1, J8.pin2
  N14: Fuse1.Connector2, J5.pin1, VCC1_6xAAA.+
  N15: S1.leg0, U1.input_voltage, J8.pin1
  N16: Power.cathode, R1.Pin_0
  N17: R2.pin_1, R3.Pin_0, Arduino_RobotDriver.A0, J1.pin2
  N18: R4.pin_1, R5.Pin_0, Arduino_RobotDriver.A1, J2.pin2
  N19: Arduino_RobotDriver.VIN, S2.leg0, J7.pin2
  N20: S2.leg1, VCC2_-_9v_block.+, J6.pin2, J7.pin1

notes:
  Right
  Left
