# Fritzing sketch Robot_PowerRegulator_v0.1 (saved by Fritzing 0.8.0b)
stripboards: 1

parts:
  C3 = Electrolytic Capacitor [capacitance=4.7mF package="100 mil [THT, electrolytic]"]
  Fuse1 = Fuse with Handler [part_number=Htc-15m]
  S1 = Pushbutton [package=THT]
  Power = LED - 5mm [color="Red (633nm)" package="5 mm [THT]"]
  U1 = Voltage Regulator - 5V [part_number=L7806CV package="TO220 [THT]"]
  R1 = Resistor [tolerance=±5% resistance=220 package=THT]
  C4 = Electrolytic Capacitor [capacitance=100nF package="100 mil [THT, electrolytic]"]
  S2 = Pushbutton [package=THT]
  VCC2_-_9v_block = Battery block 9V
  J5 = male pin header, 2 pins [form="♂ (male)"]
  J6 = male pin header, 2 pins [form="♂ (male)"]
  J7 = male pin header, 2 pins [form="♂ (male)"]
  J8 = male pin header, 2 pins [form="♂ (male)"]
  VCC1_6xAAA = Battery block 9V
  J9 = male pin header, 3 pins [form="♂ (male)"]

nets:
  GND: C3.-, U1.GND, R1.Pin_1, C4.-, VCC2_-_9v_block.-, J5.pin2, J6.pin1, VCC1_6xAAA.-, J9.pin2
  N1: C3.+, Power.anode, U1.output_voltage, C4.+, J9.pin3
  N2: Fuse1.Connector1, S1.leg1, J8.pin2
  N3: Fuse1.Connector2, J5.pin1, VCC1_6xAAA.+
  N4: S1.leg0, U1.input_voltage, J8.pin1
  N5: Power.cathode, R1.Pin_0
  N6: S2.leg0, J7.pin2, J9.pin1
  N7: S2.leg1, VCC2_-_9v_block.+, J6.pin2, J7.pin1

notes:
  Right
  Left
