# Fritzing sketch engineTest_1 (saved by Fritzing 0.7.12b)
breadboards: 1

parts:
  M1 = DC Motor
  M2 = DC Motor
  IC1 = H-Bridge [package=THT]
  Arduino1 = Arduino

nets:
  N1: M1.pin_1, IC1.4Y
  N2: M1.pin_2, IC1.3Y
  N3: M2.pin_1, IC1.1Y
  N4: M2.pin_2, IC1.2Y
  N5: IC1.1_2EN, Arduino1.D9
  N6: IC1.1A, Arduino1.D8
  GND: IC1.GND1, IC1.GND3, IC1.VCC1, Arduino1.GND
  N7: IC1.2A, Arduino1.D7
  N8: IC1.VCC2, Arduino1.+5V
  N9: IC1.3_4EN, Arduino1.D3
  N10: IC1.3A, Arduino1.D2
  N11: IC1.4A, Arduino1.D4
